// Logisim project Seperate_functions.circ as structural Verilog: 1 circuit, main circuit main
module main (
  input  [3:0] in_1,
  input  [3:0] in_2,
  input  [3:0] in_3,
  input  [3:0] in_4,
  input  [3:0] in_5,
  input  [3:0] in_6,
  input  in_7,
  output out_8,
  output [3:0] out_9,
  output [3:0] out_10,
  output [3:0] out_11,
  output [3:0] out_12
);

  wire and_1_out, and_2_out, and_3_out, and_4_out, and_5_out, and_6_out, and_7_out, and_8_out, and_9_out,
       and_10_out, and_11_out, and_12_out, and_13_out, and_14_out, and_15_out, and_16_out, and_17_out,
       and_18_out, and_19_out, and_21_out, and_22_out, and_23_out, and_24_out, not_1_out, not_2_out,
       not_3_out, not_4_out, not_5_out, not_6_out, not_7_out, not_8_out, not_9_out, not_10_out, not_11_out,
       not_12_out, or_3_out, or_4_out, or_6_out, or_8_out, xor_3_out, xor_4_out, xor_5_out, xor_7_out,
       xor_10_out, xor_11_out, xor_12_out, xor_14_out, xor_17_out, xor_18_out, xor_19_out, xor_21_out,
       xor_24_out;

  xor xor_1 (out_8, and_1_out, xor_4_out);
  and and_1 (and_1_out, 1'b0, not_1_out);
  // OR_Gate or_1 has open pins: in0=and_2_out, in4=and_5_out, out=open
  not not_1 (not_1_out, in_1[3]);
  xor xor_2 (out_9[3], xor_4_out, xor_3_out);
  // OR_Gate or_2 has open pins: in1=and_3_out, in3=and_4_out, out=open
  and and_2 (and_2_out, in_5[3], not_2_out);
  xor xor_3 (xor_3_out, not_1_out, 1'b0);
  xor xor_4 (xor_4_out, and_6_out, xor_11_out);
  and and_3 (and_3_out, in_2[3], in_3[3]);
  and and_4 (and_4_out, xor_5_out, or_4_out);
  not not_2 (not_2_out, in_4[3]);
  not not_3 (not_3_out, xor_7_out);
  and and_5 (and_5_out, or_3_out, not_3_out);
  and and_6 (and_6_out, 1'b0, not_4_out);
  xor xor_5 (xor_5_out, in_3[3], in_2[3]);
  xor xor_6 (out_10[3], or_4_out, xor_5_out);
  or or_3 (or_3_out, and_7_out, and_11_out);
  xor xor_7 (xor_7_out, in_5[3], in_4[3]);
  xor xor_8 (out_11[3], xor_7_out, or_3_out);
  not not_4 (not_4_out, in_1[2]);
  xor xor_9 (out_9[2], xor_11_out, xor_10_out);
  or or_4 (or_4_out, and_9_out, and_10_out);
  and and_7 (and_7_out, in_5[2], not_6_out);
  not not_5 (not_5_out, in_7);
  and and_8 (and_8_out, in_6[3], not_5_out);
  buf or_5 (out_12[3], and_12_out);  // OR_Gate
  xor xor_10 (xor_10_out, not_4_out, 1'b0);
  xor xor_11 (xor_11_out, and_13_out, xor_18_out);
  and and_9 (and_9_out, in_2[2], in_3[2]);
  and and_10 (and_10_out, xor_12_out, or_8_out);
  not not_6 (not_6_out, in_4[2]);
  not not_7 (not_7_out, xor_14_out);
  and and_11 (and_11_out, or_6_out, not_7_out);
  and and_12 (and_12_out, in_7, in_6[2]);
  and and_13 (and_13_out, 1'b0, not_8_out);
  xor xor_12 (xor_12_out, in_3[2], in_2[2]);
  xor xor_13 (out_10[2], or_8_out, xor_12_out);
  or or_6 (or_6_out, and_15_out, and_19_out);
  xor xor_14 (xor_14_out, in_5[2], in_4[2]);
  xor xor_15 (out_11[2], xor_14_out, or_6_out);
  and and_14 (and_14_out, in_6[2], not_5_out);
  or or_7 (out_12[2], and_8_out, and_16_out);
  not not_8 (not_8_out, in_1[1]);
  xor xor_16 (out_9[1], xor_18_out, xor_17_out);
  or or_8 (or_8_out, and_17_out, and_18_out);
  and and_15 (and_15_out, in_5[1], not_9_out);
  and and_16 (and_16_out, in_7, in_6[1]);
  xor xor_17 (xor_17_out, not_8_out, 1'b0);
  xor xor_18 (xor_18_out, and_21_out, 1'b0);
  and and_17 (and_17_out, in_2[1], in_3[1]);
  and and_18 (and_18_out, xor_19_out, and_24_out);
  not not_9 (not_9_out, in_4[1]);
  not not_10 (not_10_out, xor_21_out);
  and and_19 (and_19_out, and_22_out, not_10_out);
  and and_20 (out_12[0], in_6[1], not_5_out);
  or or_9 (out_12[1], and_14_out, and_23_out);
  and and_21 (and_21_out, 1'b1, not_11_out);
  xor xor_19 (xor_19_out, in_3[1], in_2[1]);
  xor xor_20 (out_10[1], and_24_out, xor_19_out);
  and and_22 (and_22_out, in_5[0], not_12_out);
  xor xor_21 (xor_21_out, in_5[1], in_4[1]);
  xor xor_22 (out_11[1], xor_21_out, and_22_out);
  and and_23 (and_23_out, in_7, in_6[0]);
  not not_11 (not_11_out, in_1[0]);
  xor xor_23 (out_9[0], 1'b0, xor_24_out);
  and and_24 (and_24_out, in_2[0], in_3[0]);
  not not_12 (not_12_out, in_4[0]);
  xor xor_24 (xor_24_out, not_11_out, 1'b1);
  xor xor_25 (out_10[0], in_3[0], in_2[0]);
  xor xor_26 (out_11[0], in_5[0], in_4[0]);

  // Notes on the sheet:
  //   Negating 4-bit integer
  //   Subtraction of two 4-bit integers
  //   Addition of two 4-bit integers
  //   Shifting 4-bit integer left or right
  //   0 = right
  //   1 = left
endmodule
