// Logisim project addition_subtraction.circ as structural Verilog: 1 circuit, main circuit main
module main (
  input  in_1,
  input  in_2,
  input  in_3,
  input  in_4,
  input  in_5,
  input  in_6,
  input  in_7,
  input  in_8,
  input  _8,
  input  _4,
  input  _2,
  input  _1,
  input  _8_2,
  input  _4_2,
  input  _2_2,
  input  _1_2,
  output out_17,
  output out_18,
  output out_19,
  output out_20,
  output carry
);

  wire and_1_out, and_2_out, and_3_out, and_4_out, and_5_out, and_6_out, and_7_out, and_8_out, and_9_out,
       and_10_out, and_11_out, and_12_out, and_13_out, and_14_out, not_1_out, not_2_out, not_3_out,
       not_4_out, not_5_out, not_6_out, not_7_out, or_1_out, or_2_out, xor_2_out, xor_3_out, xor_4_out,
       xor_9_out, xor_10_out, xor_11_out, xor_13_out, xor_14_out;
  wire [3:0] xor_1_out;

  xor xor_1 (xor_1_out[0], in_8, in_4);
  and and_1 (and_1_out, in_8, in_4);
  xor xor_2 (xor_2_out, in_7, in_3);
  and and_2 (and_2_out, in_7, in_3);
  xor xor_3 (xor_3_out, in_6, in_2);
  and and_3 (and_3_out, in_6, in_2);
  and and_4 (and_4_out, in_5, in_1);
  xor xor_4 (xor_4_out, in_5, in_1);
  xor xor_5 (xor_1_out[1], xor_2_out, and_1_out);
  and and_5 (and_5_out, xor_2_out, and_1_out);
  xor xor_6 (xor_1_out[2], xor_3_out, or_1_out);
  and and_6 (and_6_out, xor_3_out, or_1_out);
  xor xor_7 (xor_1_out[3], xor_4_out, or_2_out);
  and and_7 (and_7_out, xor_4_out, or_2_out);
  or or_1 (or_1_out, and_5_out, and_2_out);
  or or_2 (or_2_out, and_6_out, and_3_out);
  or or_3 (carry, and_7_out, and_4_out);
  Hex_Digit_Display hex_digit_display_1 (.value(xor_1_out));  // open: dp
  not not_1 (not_1_out, _1);
  xor xor_8 (out_20, _1, _1_2);
  and and_8 (and_8_out, not_1_out, _1_2);
  not not_2 (not_2_out, _2);
  xor xor_9 (xor_9_out, _2, _2_2);
  and and_9 (and_9_out, not_2_out, _2_2);
  not not_3 (not_3_out, _4);
  not not_4 (not_4_out, xor_9_out);
  and and_10 (and_10_out, not_4_out, and_8_out);
  xor xor_10 (xor_10_out, _4, _4_2);
  not not_5 (not_5_out, xor_10_out);
  and and_11 (and_11_out, not_3_out, _4_2);
  not not_6 (not_6_out, _8);
  and and_12 (and_12_out, not_5_out, xor_13_out);
  xor xor_11 (xor_11_out, _8, _8_2);
  not not_7 (not_7_out, xor_11_out);
  and and_13 (and_13_out, not_6_out, _8_2);
  xor xor_12 (out_19, and_8_out, xor_9_out);
  xor xor_13 (xor_13_out, and_10_out, and_9_out);
  xor xor_14 (xor_14_out, and_12_out, and_11_out);
  and and_14 (and_14_out, not_7_out, xor_14_out);
  xor xor_15 (out_18, xor_13_out, xor_10_out);
  xor xor_16 (out_17, xor_14_out, xor_11_out);
  // XOR_Gate xor_17 has open pins: in0=and_14_out, in4=and_13_out, out=open

  // Notes on the sheet:
  //   1
  //   carry
  //   2
  //   4
  //   8
  //   carry
  //   carry
  //   8
  //   4
  //   2
  //   1
endmodule
