// Logisim project calculator.circ as structural Verilog: 1 circuit, main circuit main
module main (
  input  [1:0] in_1,
  input  [3:0] in_2,
  input  [3:0] in_3,
  input  in_4,
  output carry
);

  wire and_1_out, and_2_out, and_3_out, and_4_out, and_5_out, and_6_out, and_7_out, and_8_out, and_9_out,
       and_10_out, and_11_out, and_12_out, and_13_out, and_14_out, and_15_out, and_16_out, and_17_out,
       and_18_out, and_20_out, not_1_out, not_2_out, not_3_out, not_4_out, not_5_out, not_6_out, not_7_out,
       not_8_out, or_1_out, or_2_out, xor_2_out, xor_3_out, xor_4_out, xor_9_out, xor_10_out, xor_11_out,
       xor_13_out, xor_15_out, xor_17_out;
  wire [3:0] and_19_out, demultiplexer_1_out0, demultiplexer_1_out1, demultiplexer_2_out0,
       demultiplexer_2_out1, undriven, xor_1_out, xor_8_out;

  Demultiplexer #(.select(2), .width(4)) demultiplexer_1 (
    .out0(demultiplexer_1_out0), .out1(demultiplexer_1_out1), .in(in_2), .sel(in_1));  // open: out2, out3, en
  xor xor_1 (xor_1_out[0], demultiplexer_2_out0[0], demultiplexer_1_out0[0]);
  and and_1 (and_1_out, demultiplexer_2_out0[0], demultiplexer_1_out0[0]);
  xor xor_2 (xor_2_out, demultiplexer_2_out0[1], demultiplexer_1_out0[1]);
  and and_2 (and_2_out, demultiplexer_2_out0[1], demultiplexer_1_out0[1]);
  xor xor_3 (xor_3_out, demultiplexer_2_out0[2], demultiplexer_1_out0[2]);
  and and_3 (and_3_out, demultiplexer_2_out0[2], demultiplexer_1_out0[2]);
  xor xor_4 (xor_4_out, demultiplexer_2_out0[3], demultiplexer_1_out0[3]);
  and and_4 (and_4_out, demultiplexer_2_out0[3], demultiplexer_1_out0[3]);
  xor xor_5 (xor_1_out[1], xor_2_out, and_1_out);
  and and_5 (and_5_out, xor_2_out, and_1_out);
  xor xor_6 (xor_1_out[2], xor_3_out, or_1_out);
  and and_6 (and_6_out, xor_3_out, or_1_out);
  xor xor_7 (xor_1_out[3], xor_4_out, or_2_out);
  and and_7 (and_7_out, xor_4_out, or_2_out);
  Demultiplexer #(.select(2), .width(4)) demultiplexer_2 (
    .out0(demultiplexer_2_out0), .out1(demultiplexer_2_out1), .in(in_3), .sel(in_1));  // open: out2, out3, en
  or or_1 (or_1_out, and_5_out, and_2_out);
  or or_2 (or_2_out, and_6_out, and_3_out);
  or or_3 (carry, and_7_out, and_4_out);
  not not_1 (not_1_out, demultiplexer_1_out1[0]);
  and and_8 (and_8_out, not_1_out, demultiplexer_2_out1[0]);
  not not_2 (not_2_out, demultiplexer_1_out1[1]);
  xor xor_8 (xor_8_out[0], demultiplexer_1_out1[0], demultiplexer_2_out1[0]);
  xor xor_9 (xor_9_out, demultiplexer_1_out1[1], demultiplexer_2_out1[1]);
  and and_9 (and_9_out, not_2_out, demultiplexer_2_out1[1]);
  not not_3 (not_3_out, demultiplexer_1_out1[2]);
  not not_4 (not_4_out, xor_9_out);
  xor xor_10 (xor_10_out, demultiplexer_1_out1[2], demultiplexer_2_out1[2]);
  and and_10 (and_10_out, not_3_out, demultiplexer_2_out1[2]);
  not not_5 (not_5_out, demultiplexer_1_out1[3]);
  and and_11 (and_11_out, not_4_out, and_8_out);
  not not_6 (not_6_out, xor_10_out);
  xor xor_11 (xor_11_out, demultiplexer_1_out1[3], demultiplexer_2_out1[3]);
  and and_12 (and_12_out, not_5_out, demultiplexer_2_out1[3]);
  xor xor_12 (xor_8_out[1], and_8_out, xor_9_out);
  xor xor_13 (xor_13_out, and_11_out, and_9_out);
  and and_13 (and_13_out, not_6_out, xor_13_out);
  not not_7 (not_7_out, xor_11_out);
  xor xor_14 (xor_8_out[2], xor_13_out, xor_10_out);
  xor xor_15 (xor_15_out, and_13_out, and_10_out);
  and and_14 (and_14_out, not_7_out, xor_15_out);
  xor xor_16 (xor_8_out[3], xor_15_out, xor_11_out);
  xor xor_17 (xor_17_out, and_14_out, and_12_out);
  Multiplexer #(.select(2), .width(4)) multiplexer_1 (
    .in0(xor_1_out), .in1(xor_8_out), .sel(in_1));  // open: in2, in3, out, en
  not not_8 (not_8_out, in_4);
  and and_15 (and_15_out, undriven[3], not_8_out);
  buf or_4 (and_19_out[3], and_16_out);  // OR_Gate
  and and_16 (and_16_out, in_4, undriven[2]);
  and and_17 (and_17_out, undriven[2], not_8_out);
  or or_5 (and_19_out[2], and_15_out, and_18_out);
  and and_18 (and_18_out, in_4, undriven[1]);
  or or_6 (and_19_out[1], and_17_out, and_20_out);
  and and_19 (and_19_out[0], undriven[1], not_8_out);
  and and_20 (and_20_out, in_4, undriven[0]);

  // Notes on the sheet:
  //   1
  //   carry
  //   00 - addition
  //   01 - subtraction
  //   10 - shift right
  //   11 - shift left
  //   2
  //   4
  //   8
  //   carry
  //   carry
  //   8
  //   4
  //   2
  //   1
endmodule
