// Logisim project left_right_shifter.circ as structural Verilog: 1 circuit, main circuit main
module main (
  input  _8,
  input  _4,
  input  _2,
  input  _1,
  input  in_5,
  input  [3:0] in_6,
  input  [3:0] in_7,
  input  [3:0] in_8,
  input  [1:0] in_9,
  input  [3:0] in_10
);

  wire and_1_out, and_2_out, and_3_out, and_4_out, and_6_out, not_1_out;
  wire [3:0] and_5_out, multiplexer_1_out;

  not not_1 (not_1_out, in_5);
  and and_1 (and_1_out, _8, not_1_out);
  buf or_1 (and_5_out[3], and_2_out);  // OR_Gate
  and and_2 (and_2_out, in_5, _4);
  and and_3 (and_3_out, _4, not_1_out);
  or or_2 (and_5_out[2], and_1_out, and_4_out);
  Hex_Digit_Display hex_digit_display_1 (.value(and_5_out));  // open: dp
  and and_4 (and_4_out, in_5, _2);
  or or_3 (and_5_out[1], and_3_out, and_6_out);
  Multiplexer #(.select(2), .width(4)) multiplexer_1 (
    .in0(in_6), .in1(in_7), .in2(in_8), .in3(in_10), .out(multiplexer_1_out), .sel(in_9));  // open: en
  and and_5 (and_5_out[0], _2, not_1_out);
  Hex_Digit_Display hex_digit_display_2 (.value(multiplexer_1_out));  // open: dp
  and and_6 (and_6_out, in_5, _1);

  // Notes on the sheet:
  //   0 = right
  //   1 = left
  //   8
  //   4
  //   2
  //   1
endmodule
