// Logisim project seperate_components.circ as structural Verilog: 1 circuit, main circuit main
module main (
  input  [3:0] in_1,
  input  [3:0] in_2,
  input  [3:0] in_3,
  input  [3:0] in_4,
  input  [3:0] in_5,
  input  in_6,
  output out_7,
  output out_8,
  output [3:0] out_9,
  output [3:0] out_10,
  output [3:0] out_11
);

  wire and_1_out, and_2_out, and_3_out, and_4_out, and_5_out, and_6_out, and_7_out, and_8_out, and_9_out,
       and_10_out, and_11_out, and_12_out, and_13_out, and_14_out, and_15_out, and_16_out, and_17_out,
       and_18_out, and_19_out, and_20_out, and_21_out, and_22_out, and_23_out, and_24_out, and_25_out,
       and_26_out, and_27_out, and_28_out, and_29_out, and_30_out, and_31_out, and_32_out, and_33_out,
       and_34_out, and_35_out, and_36_out, and_37_out, and_38_out, and_39_out, and_40_out, and_41_out,
       and_42_out, not_1_out, not_2_out, not_3_out, not_4_out, not_5_out, not_6_out, not_7_out, not_8_out,
       not_9_out, not_10_out, not_11_out, not_12_out, not_13_out, not_14_out, not_15_out, not_16_out,
       not_17_out, not_18_out, not_19_out, not_20_out, not_21_out, not_22_out, not_23_out, or_1_out,
       or_2_out, or_3_out, undriven, undriven_2, undriven_3, undriven_4, undriven_5, undriven_6, undriven_7,
       undriven_8, undriven_9, undriven_10, undriven_11, undriven_12, undriven_13, undriven_14, undriven_15,
       undriven_16, undriven_17, undriven_18, undriven_19, undriven_20, xor_5_out, xor_6_out, xor_7_out,
       xor_9_out, xor_10_out, xor_13_out, xor_14_out, xor_15_out, xor_16_out, xor_18_out, xor_19_out,
       xor_22_out, xor_23_out, xor_24_out, xor_25_out, xor_27_out, xor_30_out, xor_36_out, xor_38_out,
       xor_39_out, xor_41_out, xor_43_out, xor_44_out, xor_45_out, xor_47_out, xor_49_out, xor_51_out,
       xor_52_out, xor_53_out, xor_54_out, xor_56_out, xor_58_out, xor_60_out, xor_61_out;

  xor xor_1 (out_7, and_1_out, xor_6_out);
  and and_1 (and_1_out, 1'b0, not_1_out);
  // XOR_Gate xor_2 has open pins: in0=and_2_out, in4=and_5_out, out=open
  not not_1 (not_1_out, in_1[3]);
  xor xor_3 (out_9[3], xor_6_out, xor_5_out);
  // XOR_Gate xor_4 has open pins: in1=and_3_out, in3=and_4_out, out=open
  and and_2 (and_2_out, in_5[3], not_2_out);
  xor xor_5 (xor_5_out, not_1_out, 1'b0);
  xor xor_6 (xor_6_out, and_6_out, xor_15_out);
  and and_3 (and_3_out, in_2[3], in_3[3]);
  and and_4 (and_4_out, xor_7_out, xor_13_out);
  not not_2 (not_2_out, in_4[3]);
  not not_3 (not_3_out, xor_10_out);
  and and_5 (and_5_out, xor_9_out, not_3_out);
  and and_6 (and_6_out, 1'b0, not_4_out);
  xor xor_7 (xor_7_out, in_3[3], in_2[3]);
  xor xor_8 (out_10[3], xor_13_out, xor_7_out);
  xor xor_9 (xor_9_out, and_7_out, and_11_out);
  xor xor_10 (xor_10_out, in_5[3], in_4[3]);
  xor xor_11 (out_11[3], xor_10_out, xor_9_out);
  not not_4 (not_4_out, in_1[2]);
  xor xor_12 (out_9[2], xor_15_out, xor_14_out);
  xor xor_13 (xor_13_out, and_9_out, and_10_out);
  and and_7 (and_7_out, in_5[2], not_6_out);
  not not_5 (not_5_out, in_6);
  and and_8 (and_8_out, undriven, not_5_out);
  buf or_1 (or_1_out, and_12_out);  // OR_Gate
  xor xor_14 (xor_14_out, not_4_out, 1'b0);
  xor xor_15 (xor_15_out, and_13_out, xor_24_out);
  and and_9 (and_9_out, in_2[2], in_3[2]);
  and and_10 (and_10_out, xor_16_out, xor_22_out);
  not not_6 (not_6_out, in_4[2]);
  not not_7 (not_7_out, xor_19_out);
  and and_11 (and_11_out, xor_18_out, not_7_out);
  and and_12 (and_12_out, in_6, undriven_2);
  and and_13 (and_13_out, 1'b0, not_8_out);
  xor xor_16 (xor_16_out, in_3[2], in_2[2]);
  xor xor_17 (out_10[2], xor_22_out, xor_16_out);
  xor xor_18 (xor_18_out, and_15_out, and_19_out);
  xor xor_19 (xor_19_out, in_5[2], in_4[2]);
  xor xor_20 (out_11[2], xor_19_out, xor_18_out);
  and and_14 (and_14_out, undriven_2, not_5_out);
  or or_2 (or_2_out, and_8_out, and_16_out);
  not not_8 (not_8_out, in_1[1]);
  xor xor_21 (out_9[1], xor_24_out, xor_23_out);
  xor xor_22 (xor_22_out, and_17_out, and_18_out);
  and and_15 (and_15_out, in_5[1], not_9_out);
  and and_16 (and_16_out, in_6, undriven_3);
  xor xor_23 (xor_23_out, not_8_out, 1'b0);
  xor xor_24 (xor_24_out, and_21_out, 1'b0);
  and and_17 (and_17_out, in_2[1], in_3[1]);
  and and_18 (and_18_out, xor_25_out, and_24_out);
  not not_9 (not_9_out, in_4[1]);
  not not_10 (not_10_out, xor_27_out);
  and and_19 (and_19_out, and_22_out, not_10_out);
  and and_20 (and_20_out, undriven_3, not_5_out);
  or or_3 (or_3_out, and_14_out, and_23_out);
  and and_21 (and_21_out, 1'b1, not_11_out);
  xor xor_25 (xor_25_out, in_3[1], in_2[1]);
  xor xor_26 (out_10[1], and_24_out, xor_25_out);
  and and_22 (and_22_out, in_5[0], not_12_out);
  xor xor_27 (xor_27_out, in_5[1], in_4[1]);
  xor xor_28 (out_11[1], xor_27_out, and_22_out);
  and and_23 (and_23_out, in_6, undriven_4);
  not not_11 (not_11_out, in_1[0]);
  xor xor_29 (out_9[0], 1'b0, xor_30_out);
  and and_24 (and_24_out, in_2[0], in_3[0]);
  not not_12 (not_12_out, in_4[0]);
  xor xor_30 (xor_30_out, not_11_out, 1'b1);
  xor xor_31 (out_10[0], in_3[0], in_2[0]);
  xor xor_32 (out_11[0], in_5[0], in_4[0]);
  xor xor_33 (out_8, and_25_out, xor_38_out);
  and and_25 (and_25_out, 1'b0, not_13_out);
  // XOR_Gate xor_34 has open pins: in1=and_26_out, in3=and_27_out, out=open
  // XOR_Gate xor_35 has open pins: in0=and_28_out, in4=and_29_out, out=open
  // NOT_Gate not_13 has open pins: in=open, out=not_13_out
  xor xor_36 (xor_36_out, not_13_out, 1'b0);
  // XOR_Gate xor_37 has open pins: in3=xor_38_out, in4=xor_36_out, out=open
  and and_26 (and_26_out, undriven_5, undriven_6);
  and and_27 (and_27_out, xor_39_out, xor_43_out);
  not not_14 (not_14_out, undriven_8);
  and and_28 (and_28_out, undriven_7, not_14_out);
  and and_29 (and_29_out, xor_44_out, not_15_out);
  xor xor_38 (xor_38_out, and_30_out, xor_47_out);
  xor xor_39 (xor_39_out, undriven_6, undriven_5);
  // XOR_Gate xor_40 has open pins: in0=xor_43_out, in4=xor_39_out, out=open
  xor xor_41 (xor_41_out, undriven_7, undriven_8);
  not not_15 (not_15_out, xor_41_out);
  // XOR_Gate xor_42 has open pins: in0=xor_41_out, in4=xor_44_out, out=open
  and and_30 (and_30_out, 1'b0, not_16_out);
  xor xor_43 (xor_43_out, and_31_out, and_32_out);
  xor xor_44 (xor_44_out, and_33_out, and_34_out);
  // NOT_Gate not_16 has open pins: in=open, out=not_16_out
  xor xor_45 (xor_45_out, not_16_out, 1'b0);
  // XOR_Gate xor_46 has open pins: in3=xor_47_out, in4=xor_45_out, out=open
  and and_31 (and_31_out, undriven_9, undriven_10);
  and and_32 (and_32_out, xor_52_out, xor_51_out);
  not not_17 (not_17_out, undriven_12);
  and and_33 (and_33_out, undriven_11, not_17_out);
  and and_34 (and_34_out, xor_53_out, not_18_out);
  xor xor_47 (xor_47_out, and_35_out, xor_56_out);
  // XOR_Gate xor_48 has open pins: in0=xor_51_out, in4=xor_52_out, out=open
  xor xor_49 (xor_49_out, undriven_11, undriven_12);
  not not_18 (not_18_out, xor_49_out);
  // XOR_Gate xor_50 has open pins: in0=xor_49_out, in4=xor_53_out, out=open
  and and_35 (and_35_out, 1'b0, not_19_out);
  xor xor_51 (xor_51_out, and_36_out, and_37_out);
  xor xor_52 (xor_52_out, undriven_10, undriven_9);
  xor xor_53 (xor_53_out, and_38_out, and_39_out);
  // NOT_Gate not_19 has open pins: in=open, out=not_19_out
  xor xor_54 (xor_54_out, not_19_out, 1'b0);
  // XOR_Gate xor_55 has open pins: in3=xor_56_out, in4=xor_54_out, out=open
  and and_36 (and_36_out, undriven_13, undriven_14);
  and and_37 (and_37_out, xor_60_out, and_41_out);
  not not_20 (not_20_out, undriven_16);
  and and_38 (and_38_out, undriven_15, not_20_out);
  and and_39 (and_39_out, and_42_out, not_21_out);
  xor xor_56 (xor_56_out, and_40_out, 1'b0);
  // XOR_Gate xor_57 has open pins: in0=and_41_out, in4=xor_60_out, out=open
  xor xor_58 (xor_58_out, undriven_15, undriven_16);
  not not_21 (not_21_out, xor_58_out);
  // XOR_Gate xor_59 has open pins: in0=xor_58_out, in4=and_42_out, out=open
  and and_40 (and_40_out, 1'b1, not_22_out);
  and and_41 (and_41_out, undriven_18, undriven_19);
  xor xor_60 (xor_60_out, undriven_14, undriven_13);
  and and_42 (and_42_out, undriven_17, not_23_out);
  // NOT_Gate not_22 has open pins: in=open, out=not_22_out
  xor xor_61 (xor_61_out, not_22_out, 1'b1);
  // XOR_Gate xor_62 has open pins: in3=1'b0, in4=xor_61_out, out=open
  // XOR_Gate xor_63 has open pins: in0=undriven_19, in4=undriven_18, out=open
  not not_23 (not_23_out, undriven_20);
  // XOR_Gate xor_64 has open pins: in0=undriven_17, in4=undriven_20, out=open

  // Notes on the sheet:
  //   0 = right
  //   1 = left
endmodule
